# Fritzing sketch LCD-I2C (saved by Fritzing 0.9.3b)

parts:
  Grove1 = Grove RGB LCD
  パーツ1 = Arduino Uno (Rev3)

nets:
  GND: Grove1.GND, パーツ1.GND
  VCC: Grove1.VCC, パーツ1.5V
  N1: Grove1.SDA, パーツ1.A4/SDA
  N2: Grove1.SCL, パーツ1.A5/SCL
