# Fritzing sketch LCD-backlight (saved by Fritzing 0.9.3b)
breadboards: 1

parts:
  パーツ1 = Arduino Uno (Rev3)
  LCD1 = LCD screen
  R1 = Trimmer Potentiometer [maximum_resistance=10kΩ package=THT]

nets:
  N1: パーツ1.D8, LCD1.E
  N2: パーツ1.D9_PWM, LCD1.DB4
  N3: パーツ1.D10_PWM/SS, LCD1.DB5
  N4: パーツ1.D11_PWM/MOSI, LCD1.DB6
  N5: パーツ1.D12/MISO, LCD1.DB7
  N6: パーツ1.D13/SCK, LCD1.LED+
  GND: パーツ1.GND, LCD1.VSS, LCD1.R/W, LCD1.LED-, R1.leg2
  N7: パーツ1.D7, LCD1.RS
  5V: パーツ1.5V, LCD1.VDD, R1.leg1
  N8: LCD1.V0, R1.wiper
