# Fritzing sketch adxl335 (saved by Fritzing 0.9.3b)

parts:
  パーツ1 = Triple Axis Accelerometer Breakout - ADXL335
  パーツ2 = Arduino Uno (Rev3)

nets:
  N1: パーツ1.ZOUT, パーツ2.A2
  N2: パーツ1.YOUT, パーツ2.A1
  N3: パーツ1.XOUT, パーツ2.A0
  GND: パーツ1.GND, パーツ2.GND
  VCC: パーツ1.VCC, パーツ2.5V
