# Fritzing sketch button-9 (saved by Fritzing 0.9.3b)
breadboards: 1

parts:
  パーツ1 = Arduino Uno (Rev3)
  S1 = Pushbutton [package="[THT]"]
  R1 = Resistor [tolerance=±5% resistance=220 package=THT]

nets:
  N1: パーツ1.D9_PWM, S1.Pin_3, S1.Pin_4, R1.Pin_1
  N2: パーツ1.GND, S1.Pin_1, S1.Pin_2
  N3: パーツ1.5V, R1.Pin_0
