# Fritzing sketch button-active-low2 (saved by Fritzing 0.9.3b)
breadboards: 1

parts:
  パーツ1 = Arduino Uno (Rev3)
  S1 = Pushbutton [package="[THT]"]

nets:
  N1: パーツ1.GND, S1.Pin_3, S1.Pin_4
  N2: パーツ1.D2, S1.Pin_1, S1.Pin_2
