# Fritzing sketch expander-PCF8575 (saved by Fritzing 0.9.3b)
breadboards: 1

parts:
  Part1 = Arduino Uno (Rev3)
  IC2 = PCF8575
  S1 = Pushbutton [package="[THT]"]
  R1 = Resistor [tolerance=±5% resistance=220 package=THT]
  LED1 = LED - 5mm [color="Red (633nm)" package="5 mm [THT]"]

nets:
  N1: Part1.A4/SDA, IC2.SDA
  N2: Part1.A5/SCL, IC2.SCL
  GND: Part1.GND, IC2.GND, R1.Pin_0, LED1.cathode
  5V: Part1.5V, IC2.VCC, S1.Pin_1, S1.Pin_2
  N3: IC2.GPB7, S1.Pin_3, S1.Pin_4, R1.Pin_1
  N4: IC2.GPA0, LED1.anode
