# Fritzing sketch gps (saved by Fritzing 0.9.3b)

parts:
  U1 = Generic GPS
  Part1 = Arduino Uno (Rev3)

nets:
  N1: U1.RX, Part1.D10_PWM/SS
  N2: U1.TX, Part1.D11_PWM/MOSI
  GND: U1.GND, Part1.GND
  VCC: U1.VCC, Part1.5V
