# Fritzing sketch hcsr04 (saved by Fritzing 0.9.3b)

parts:
  パーツ1 = Arduino Uno (Rev3)
  hc-sr1 = hc-sr04

nets:
  GND: パーツ1.GND, hc-sr1.GND
  N1: パーツ1.D7, hc-sr1.Trig, hc-sr1.Echo
  5V: パーツ1.5V, hc-sr1.VCC
