# Fritzing sketch hmc5883l (saved by Fritzing 0.9.3b)

parts:
  パーツ1 = Triple Axis Magnetometer - HMC5883 Breakout
  パーツ2 = Arduino Uno (Rev3)

nets:
  GND: パーツ1.GND, パーツ2.GND
  VCC: パーツ1.VCC, パーツ2.5V
  N1: パーツ1.SDA, パーツ2.A4/SDA
  N2: パーツ1.SCL, パーツ2.A5/SCL
