# Fritzing sketch joystick (saved by Fritzing 0.9.3b)

parts:
  U1 = JOYSTICK-PSP1000 [package=joystick-psp1000]
  パーツ1 = Arduino Uno (Rev3)

nets:
  GND: U1.GND, パーツ1.GND
  VCC: U1.VCC, パーツ1.5V
  N1: U1.X, パーツ1.A0
  N2: U1.Y, パーツ1.A1
