# Fritzing sketch led-9 (saved by Fritzing 0.9.3b)

parts:
  パーツ1 = Arduino Uno (Rev3)
  LED1 = LED - 5mm [color="Red (633nm)" package="5 mm [THT]"]

nets:
  N1: パーツ1.D9_PWM, LED1.anode
  N2: パーツ1.GND, LED1.cathode
