# Fritzing sketch led-array (saved by Fritzing 0.9.3b)
breadboards: 1

parts:
  パーツ1 = Arduino Uno (Rev3)
  LED1 = LED - 5mm [color="Blue (525nm)" package="5 mm [THT]"]
  LED2 = LED - 5mm [color="Green (570nm)" package="5 mm [THT]"]
  LED3 = LED - 5mm [color="Red (633nm)" package="5 mm [THT]"]

nets:
  N1: パーツ1.D9_PWM, LED3.anode
  N2: パーツ1.D10_PWM/SS, LED2.anode
  N3: パーツ1.D11_PWM/MOSI, LED1.anode
  N4: パーツ1.GND, LED1.cathode, LED2.cathode, LED3.cathode
