# Fritzing sketch led-digits-HT16K33 (saved by Fritzing 0.9.3b)

parts:
  7SEG3 = 7-Segment LED I2C Backpack (white)
  Part1 = Arduino Uno (Rev3) - ICSP

nets:
  N1: 7SEG3.V+, Part1.5V
  GND: 7SEG3.GND, Part1.GND
  N2: 7SEG3.SDA, Part1.A4/SDA
  N3: 7SEG3.SCL, Part1.A5/SCL

custom parts:
  7-Segment LED I2C Backpack (white): 4-digit, 7-segment LED Display with I2C Control
