# Fritzing sketch led-digits (saved by Fritzing 0.9.3b)

parts:
  Part1 = Arduino Uno (Rev3)
  U2 = MAX7219 [package=dil24]

nets (from the breadboard view):
  GND: Part1.GND, U2.GND
  N1: Part1.D2, U2.DIN
  N2: Part1.D3_PWM, U2.CLK
  N3: Part1.D4, U2.CS
  5V: Part1.5V, U2.VCC

custom parts:
  MAX7219: 8-digit, 8-segment LED display driver, serial input
