# Fritzing sketch led-matrix-HT16K33 (saved by Fritzing 0.9.3b)

parts:
  Part1 = Arduino Uno (Rev3)
  LED2 = 8x8 LED Matrix (yellow)

nets:
  N1: Part1.A4/SDA, LED2.D
  N2: Part1.A5/SCL, LED2.C
  N3: Part1.GND, LED2.-
  N4: Part1.5V, LED2.+

custom parts:
  8x8 LED Matrix (yellow): 8x8 LED Matrix with I2C control (yellow)
