# Fritzing sketch led-matrix (saved by Fritzing 0.9.3b)

parts:
  Part1 = Arduino Uno (Rev3)
  Part3 = LED Matrix - Serial Interface - Red/Green/Blue

nets:
  N1: Part1.D2, Part3.MISO
  N2: Part1.D3_PWM, Part3.SCK
  N3: Part1.D4, Part3.CS
  5V: Part1.5V, Part3.VCC
  GND: Part1.GND, Part3.GND
