# Fritzing sketch led-rgb-anode (saved by Fritzing 0.9.3b)
breadboards: 1

parts:
  パーツ1 = Arduino Uno (Rev3)
  LED1 = RGB LED - (4 legs) [package="5 mm [THT]"]
  R1 = Resistor [tolerance=±5% resistance=220 package=THT]
  R2 = Resistor [tolerance=±5% resistance=220 package=THT]
  R3 = Resistor [tolerance=±5% resistance=220 package=THT]

nets:
  N1: パーツ1.D3_PWM, R3.Pin_1
  N2: パーツ1.D5_PWM, R2.Pin_1
  N3: パーツ1.D6_PWM, R1.Pin_1
  N4: パーツ1.5V, LED1.common_anode
  N5: LED1.red_cathode, R1.Pin_0
  N6: LED1.green_cathode, R2.Pin_0
  N7: LED1.blue_cathode, R3.Pin_0
