# Fritzing sketch led-rgb (saved by Fritzing 0.9.3b)
breadboards: 1

parts:
  パーツ1 = Arduino Uno (Rev3)
  LED1 = RGB LED (com. cathode, rgb) [package="5 mm [THT]"]

nets:
  N1: パーツ1.GND, LED1.common_cathode
  N2: パーツ1.D3_PWM, LED1.blue_anode
  N3: パーツ1.D5_PWM, LED1.green_anode
  N4: パーツ1.D6_PWM, LED1.red_anode
