# Fritzing sketch motor (saved by Fritzing 0.9.3b)

parts:
  パーツ3 = Arduino Motor Shield (Rev3)
  M1 = DC Motor
  VCC1 = 4 x AAA Battery Mount

nets:
  N1: パーツ3.A-, M1.pin_2
  N2: パーツ3.A+, M1.pin_1
  N3: パーツ3.VMOT, VCC1.+
  N4: パーツ3.GND, VCC1.-
