# Fritzing sketch photoreistor (saved by Fritzing 0.9.3b)
breadboards: 1

parts:
  R1 = Photocell (LDR) [package=THT]
  パーツ1 = Arduino Uno (Rev3)
  R2 = Resistor [tolerance=±5% resistance=10k package=THT]

nets:
  N1: R1.pin_0, パーツ1.GND
  N2: R1.pin_1, パーツ1.A0, R2.Pin_1
  N3: パーツ1.5V, R2.Pin_0
