# Fritzing sketch relay-nc (saved by Fritzing 0.9.3b)

parts:
  Power_plug1 = Power plug
  U2 = V18ZA2P [package=v18za2p]
  KY-1 = Keyes Relay [package=THT]
  Part1 = Arduino Uno (Rev3)

nets:
  N1: Power_plug1.GND, U2.-
  N2: Power_plug1.VCC, KY-1.NC
  N3: U2.+, KY-1.C
  N4: KY-1.signal, Part1.D10_PWM/SS
  N5: KY-1.power, Part1.5V
  N6: KY-1.ground, Part1.GND

custom parts:
  V18ZA2P: Varistor
  Keyes Relay: The Keyes 5V relay module is suitable for SCM development, home appliance control. It uses a 5V~12V TIL control signal which can control DC / AC signal.
