# Fritzing sketch sensor-Potentiometer (saved by Fritzing 0.9.3b)

parts:
  R1 = Rotary Potentiometer (Small) [maximum_resistance=100kΩ package=THT]
  パーツ1 = Arduino Uno (Rev3)

nets:
  N1: R1.leg1, パーツ1.GND
  N2: R1.wiper, パーツ1.A0
  N3: R1.leg2, パーツ1.5V
