# Fritzing sketch switch-nc (saved by Fritzing 0.9.3b)
breadboards: 1

parts:
  S1 = Toggle Switch [package=THT]
  パーツ1 = Arduino Uno (Rev3)
  R1 = Resistor [tolerance=±5% resistance=10k package=THT]

nets:
  N1: S1.L1, パーツ1.GND
  N2: S1.COM, パーツ1.D8, R1.Pin_0
  N3: パーツ1.5V, R1.Pin_1
