# Fritzing sketch tmp36 (saved by Fritzing 0.9.3b)
breadboards: 1

parts:
  パーツ1 = Arduino Uno (Rev3)
  T2 = TMP36 Temperature Sensor [package="TO92 [THT]"]

nets:
  N1: パーツ1.A0, T2.Vout
  GND: パーツ1.GND, T2.GND
  N2: パーツ1.5V, T2.+Vs
